// Logisim project lab.circ as structural Verilog: 2 circuits, main circuit main
module main (
  input  [1:0] xrow,
  input  [1:0] xcol,
  input  [2:0] r1,
  input  [3:0] r2,
  input  [2:0] r3,
  input  [3:0] r4,
  input  [2:0] r5,
  input  [3:0] r6,
  input  [2:0] r7,
  output [1:0] out_10,
  output [1:0] out_11
);

  wire active, clk, decoder_1_out0, decoder_1_out1, decoder_1_out2, decoder_1_out3, rst, start;
  wire [8:0] field_1_out_8, field_1_out_9, field_1_out_10, field_1_out_11, field_1_out_12, field_1_out_13,
       field_1_out_14, field_1_out_15, field_1_out_16;

  Clock u_clk (.out(clk));
  Button u_rst (.out(rst));
  Button u_start (.out(start));
  LED led_1 (.in(active));
  Decoder #(.select(2), .disabled(0), .enable("false")) decoder_1 (
    .out0(decoder_1_out0), .out1(decoder_1_out1), .out2(decoder_1_out2), .out3(decoder_1_out3));  // open: sel
  LED led_2 (.in(decoder_1_out0));
  LED led_3 (.in(decoder_1_out2));
  LED led_4 (.in(decoder_1_out3));
  LED led_5 (.in(decoder_1_out1));
  DotMatrix #(.inputtype("row"), .matrixcols(9), .matrixrows(9)) dotmatrix_1 (
    .row0(field_1_out_8), .row1(field_1_out_9), .row2(field_1_out_10), .row3(field_1_out_11),
    .row4(field_1_out_12), .row5(field_1_out_13), .row6(field_1_out_14), .row7(field_1_out_15),
    .row8(field_1_out_16));
  field field_1 (
    .in_1(r1), .in_2(r2), .in_3(r3), .in_4(r4), .in_5(r5), .in_6(r6), .in_7(r7), .out_8(field_1_out_8),
    .out_9(field_1_out_9), .out_10(field_1_out_10), .out_11(field_1_out_11), .out_12(field_1_out_12),
    .out_13(field_1_out_13), .out_14(field_1_out_14), .out_15(field_1_out_15), .out_16(field_1_out_16));

  // Other names for the same wires on the sheet: col[1:0] = out_11; row[1:0] = out_10
endmodule

module field (
  input  [2:0] in_1,
  input  [3:0] in_2,
  input  [2:0] in_3,
  input  [3:0] in_4,
  input  [2:0] in_5,
  input  [3:0] in_6,
  input  [2:0] in_7,
  output [8:0] out_8,
  output [8:0] out_9,
  output [8:0] out_10,
  output [8:0] out_11,
  output [8:0] out_12,
  output [8:0] out_13,
  output [8:0] out_14,
  output [8:0] out_15,
  output [8:0] out_16
);


  assign out_8 = {9{1'b0}};
  assign out_9 = {2'b01, in_1[2], 1'b1, in_1[1], 1'b1, in_1[0], 2'b10};
  assign out_10 = {1'b0, in_2[3], 1'b0, in_2[2], 1'b0, in_2[1], 1'b0, in_2[0], 1'b0};
  assign out_11 = {2'b01, in_3[2], 1'b1, in_3[1], 1'b1, in_3[0], 2'b10};
  assign out_12 = {1'b0, in_4[3], 1'b0, in_4[2], 1'b0, in_4[1], 1'b0, in_4[0], 1'b0};
  assign out_13 = {2'b01, in_5[2], 1'b1, in_5[1], 1'b1, in_5[0], 2'b10};
  assign out_14 = {1'b0, in_6[3], 1'b0, in_6[2], 1'b0, in_6[1], 1'b0, in_6[0], 1'b0};
  assign out_15 = {2'b01, in_7[2], 1'b1, in_7[1], 1'b1, in_7[0], 2'b10};
  assign out_16 = {9{1'b0}};
endmodule
