// Logisim project lab_solution.circ as structural Verilog: 2 circuits, main circuit main
module main (
  input  [1:0] xrow,
  input  [1:0] xcol,
  input  [2:0] r1,
  input  [3:0] r2,
  input  [2:0] r3,
  input  [3:0] r4,
  input  [2:0] r5,
  input  [3:0] r6,
  input  [2:0] r7,
  output [1:0] out_10,
  output [1:0] out_11
);

  wire active, and_1_out, and_2_out, and_3_out, and_4_out, and_5_out, and_6_out, and_7_out, and_8_out,
       and_9_out, and_10_out, and_11_out, and_12_out, and_13_out, and_14_out, and_15_out, and_16_out,
       and_17_out, and_18_out, and_19_out, and_20_out, and_21_out, clk, comparator_1_eq, comparator_2_eq,
       decoder_1_out0, decoder_1_out1, decoder_1_out2, decoder_1_out3, not_1_out, not_2_out, not_3_out,
       not_4_out, not_5_out, not_6_out, not_7_out, not_8_out, not_9_out, not_10_out, not_11_out, not_12_out,
       not_13_out, not_14_out, not_15_out, not_16_out, not_17_out, not_18_out, not_19_out, not_20_out,
       or_5_out, rst, start;
  wire [1:0] adder_1_out, adder_2_out, bitfinder_1_index, dir, multiplexer_4_out, multiplexer_4_out_2,
       multiplexer_4_out_3, multiplexer_4_out_4, multiplexer_5_out, multiplexer_6_out, multiplexer_7_out,
       multiplexer_8_out, multiplexer_9_out, multiplexer_10_out, multiplexer_11_out, subtractor_1_out,
       subtractor_2_out;
  wire [2:0] multiplexer_3_out;
  wire [3:0] bitselector_4_out, multiplexer_1_out, multiplexer_2_out, or_1_out, shifter_1_out, shifter_2_out,
       shifter_3_out, shifter_4_out, shifter_5_out, shifter_6_out, shifter_7_out, shifter_8_out,
       shifter_9_out;
  wire [8:0] field_1_out_8, field_1_out_9, field_1_out_10, field_1_out_11, field_1_out_12, field_1_out_13,
       field_1_out_14, field_1_out_15, field_1_out_16;

  Clock u_clk (.out(clk));
  Button u_rst (.out(rst));
  Button u_start (.out(start));
  LED led_1 (.in(active));
  Decoder #(.select(2), .disabled(0), .enable("false")) decoder_1 (
    .out0(decoder_1_out0), .out1(decoder_1_out1), .out2(decoder_1_out2), .out3(decoder_1_out3), .sel(dir));
  Multiplexer #(.select(2), .width(4), .enable("false")) multiplexer_1 (
    .in0(4'b0000), .in1(r2), .in2(r4), .in3(r6), .out(multiplexer_1_out), .sel(out_10));
  Multiplexer #(.select(2), .width(4), .enable("false")) multiplexer_2 (
    .in0(r2), .in1(r4), .in2(r6), .in3(4'b0000), .out(multiplexer_2_out), .sel(out_10));
  // Probe on multiplexer_4_out_4
  // Probe on multiplexer_4_out_3
  // Probe on multiplexer_4_out_2
  // Probe on multiplexer_4_out
  LED led_2 (.in(decoder_1_out0));
  LED led_3 (.in(decoder_1_out2));
  LED led_4 (.in(decoder_1_out3));
  LED led_5 (.in(decoder_1_out1));
  field field_1 (
    .in_1(r1), .in_2(r2), .in_3(r3), .in_4(r4), .in_5(r5), .in_6(r6), .in_7(r7), .out_8(field_1_out_8),
    .out_9(field_1_out_9), .out_10(field_1_out_10), .out_11(field_1_out_11), .out_12(field_1_out_12),
    .out_13(field_1_out_13), .out_14(field_1_out_14), .out_15(field_1_out_15), .out_16(field_1_out_16));
  DotMatrix #(.inputtype("row"), .matrixcols(9), .matrixrows(9)) dotmatrix_1 (
    .row0(field_1_out_8), .row1(field_1_out_9), .row2(field_1_out_10), .row3(field_1_out_11),
    .row4(field_1_out_12), .row5(field_1_out_13), .row6(field_1_out_14), .row7(field_1_out_15),
    .row8(field_1_out_16));
  Multiplexer #(.select(2), .width(3), .disabled(0), .enable("false")) multiplexer_3 (
    .in0(r1), .in1(r3), .in2(r5), .in3(r7), .out(multiplexer_3_out), .sel(out_10));
  // Probe on multiplexer_1_out
  not not_1 (not_1_out, multiplexer_4_out_4[0]);
  not not_2 (not_2_out, multiplexer_4_out_4[0]);
  not not_3 (not_3_out, multiplexer_4_out_4[1]);
  not not_4 (not_4_out, multiplexer_4_out_4[1]);
  not not_5 (not_5_out, multiplexer_4_out_3[0]);
  not not_6 (not_6_out, multiplexer_4_out_3[0]);
  not not_7 (not_7_out, multiplexer_4_out_3[1]);
  not not_8 (not_8_out, multiplexer_4_out_3[1]);
  not not_9 (not_9_out, multiplexer_4_out_2[0]);
  not not_10 (not_10_out, multiplexer_4_out_2[0]);
  not not_11 (not_11_out, multiplexer_4_out_2[1]);
  not not_12 (not_12_out, multiplexer_4_out_2[1]);
  not not_13 (not_13_out, multiplexer_4_out[0]);
  not not_14 (not_14_out, multiplexer_4_out[0]);
  not not_15 (not_15_out, multiplexer_4_out[1]);
  not not_16 (not_16_out, multiplexer_4_out[1]);
  // Probe on multiplexer_3_out
  // Probe on {1'b0, multiplexer_3_out}
  // Probe on multiplexer_2_out
  and and_1 (and_1_out, bitselector_4_out[0], not_1_out, multiplexer_4_out_4[1]);
  and and_2 (and_2_out, multiplexer_4_out_4[0], multiplexer_4_out_4[1], bitselector_4_out[1]);
  or or_1 (or_1_out[0], and_1_out, and_2_out, and_3_out, and_4_out);
  and and_3 (and_3_out, bitselector_4_out[2], not_2_out, not_3_out);
  and and_4 (and_4_out, multiplexer_4_out_4[0], not_4_out, bitselector_4_out[3]);
  and and_5 (and_5_out, bitselector_4_out[0], not_5_out, multiplexer_4_out_3[1]);
  and and_6 (and_6_out, multiplexer_4_out_3[0], multiplexer_4_out_3[1], bitselector_4_out[1]);
  or or_2 (or_1_out[1], and_5_out, and_6_out, and_7_out, and_8_out);
  and and_7 (and_7_out, bitselector_4_out[2], not_6_out, not_7_out);
  and and_8 (and_8_out, multiplexer_4_out_3[0], not_8_out, bitselector_4_out[3]);
  and and_9 (and_9_out, bitselector_4_out[0], not_9_out, multiplexer_4_out_2[1]);
  and and_10 (and_10_out, multiplexer_4_out_2[0], multiplexer_4_out_2[1], bitselector_4_out[1]);
  or or_3 (or_1_out[2], and_9_out, and_10_out, and_11_out, and_12_out);
  and and_11 (and_11_out, bitselector_4_out[2], not_10_out, not_11_out);
  and and_12 (and_12_out, multiplexer_4_out_2[0], not_12_out, bitselector_4_out[3]);
  and and_13 (and_13_out, bitselector_4_out[0], not_13_out, multiplexer_4_out[1]);
  and and_14 (and_14_out, multiplexer_4_out[0], multiplexer_4_out[1], bitselector_4_out[1]);
  or or_4 (or_1_out[3], and_13_out, and_14_out, and_15_out, and_16_out);
  and and_15 (and_15_out, bitselector_4_out[2], not_14_out, not_15_out);
  and and_16 (and_16_out, multiplexer_4_out[0], not_16_out, bitselector_4_out[3]);
  Register #(.width(2)) row (.D(multiplexer_7_out), .en(active), .Q(out_10), .clk(clk), .clr(rst));
  Shifter #(.width(4), .shift("rl")) shifter_1 (.in({1'b0, multiplexer_3_out}), .\dist (2'b01), .out(shifter_1_out));
  Shifter #(.width(4), .shift("rl")) shifter_2 (.in({1'b0, multiplexer_3_out}), .\dist (out_11), .out(shifter_2_out));
  Shifter #(.width(4), .shift("rl")) shifter_3 (.in(multiplexer_1_out), .\dist (out_11), .out(shifter_3_out));
  Shifter #(.width(4), .shift("rl")) shifter_4 (.in(multiplexer_2_out), .\dist (out_11), .out(shifter_4_out));
  // Probe on or_1_out
  or or_5 (or_5_out, rst, and_17_out);
  Comparator #(.width(2), .mode("unsigned")) comparator_1 (.a(xrow), .b(out_10), .eq(comparator_1_eq));  // open: gt, lt
  Comparator #(.width(2), .mode("unsigned")) comparator_2 (.a(xcol), .b(out_11), .eq(comparator_2_eq));  // open: gt, lt
  Register #(.width(2)) col (.D(multiplexer_6_out), .en(active), .Q(out_11), .clk(clk), .clr(rst));
  Shifter #(.width(4), .shift("rl")) shifter_5 (.in(shifter_1_out), .\dist (out_11), .out(shifter_5_out));
  Shifter #(.width(4), .shift("lr")) shifter_6 (.in(shifter_2_out), .\dist (2'b11), .out(shifter_6_out));
  BitSelector #(.width(4)) bitselector_1 (.in(shifter_6_out), .out(bitselector_4_out[1]), .sel(2'b00));
  BitSelector #(.width(4)) bitselector_2 (.in(shifter_7_out), .out(bitselector_4_out[2]), .sel(2'b00));
  Shifter #(.width(4), .shift("lr")) shifter_7 (.in(shifter_3_out), .\dist (2'b11), .out(shifter_7_out));
  Shifter #(.width(4), .shift("lr")) shifter_8 (.in(shifter_4_out), .\dist (2'b11), .out(shifter_8_out));
  BitSelector #(.width(4)) bitselector_3 (.in(shifter_8_out), .out(bitselector_4_out[3]), .sel(2'b00));
  BitFinder #(.width(4)) bitfinder_1 (.in(or_1_out), .index(bitfinder_1_index));  // open: found
  D_Flip_Flop u_active (.Q(active), .preset(start), .reset(or_5_out));  // open: clk, D, Qn, en
  Register #(.width(2)) u_dir (.D(multiplexer_5_out), .en(active), .Q(dir), .clk(clk), .clr(rst));
  // Probe on {multiplexer_4_out_4, multiplexer_4_out_3, multiplexer_4_out_2, multiplexer_4_out}
  // Probe on multiplexer_4_out_3
  // Probe on multiplexer_4_out_4
  // Probe on multiplexer_4_out_2
  Shifter #(.width(4), .shift("lr")) shifter_9 (.in(shifter_5_out), .\dist (2'b11), .out(shifter_9_out));
  and and_17 (and_17_out, comparator_1_eq, comparator_2_eq);
  Multiplexer #(.select(2), .width(8), .enable("false")) multiplexer_4 (
    .in0(8'h2d), .in1(8'h78), .in2(8'h93), .in3(8'hc6),
    .out({multiplexer_4_out_4, multiplexer_4_out_3, multiplexer_4_out_2, multiplexer_4_out}), .sel(dir));
  // Probe on multiplexer_4_out
  BitSelector #(.width(4)) bitselector_4 (.in(shifter_9_out), .out(bitselector_4_out[0]), .sel(2'b00));
  not not_17 (not_17_out, multiplexer_5_out[0]);
  and and_18 (and_18_out, bitselector_4_out[0], not_17_out, multiplexer_5_out[1]);
  and and_19 (and_19_out, multiplexer_5_out[0], multiplexer_5_out[1], bitselector_4_out[1]);
  and and_20 (and_20_out, bitselector_4_out[2], not_18_out, not_19_out);
  not not_18 (not_18_out, multiplexer_5_out[0]);
  not not_19 (not_19_out, multiplexer_5_out[1]);
  not not_20 (not_20_out, multiplexer_5_out[1]);
  and and_21 (and_21_out, multiplexer_5_out[0], not_20_out, bitselector_4_out[3]);
  Multiplexer #(.select(2), .width(2), .enable("false")) multiplexer_5 (
    .in0(multiplexer_4_out_4), .in1(multiplexer_4_out_3), .in2(multiplexer_4_out_2), .in3(multiplexer_4_out),
    .out(multiplexer_5_out), .sel(bitfinder_1_index));
  Multiplexer #(.select(2), .width(2), .enable("false")) multiplexer_6 (
    .in0(out_11), .in1(out_11), .in2(multiplexer_8_out), .in3(multiplexer_9_out), .out(multiplexer_6_out),
    .sel(multiplexer_5_out));
  Multiplexer #(.select(2), .width(2), .enable("false")) multiplexer_7 (
    .in0(multiplexer_10_out), .in1(multiplexer_11_out), .in2(out_10), .in3(out_10), .out(multiplexer_7_out),
    .sel(multiplexer_5_out));
  // Probe on multiplexer_5_out
  Multiplexer #(.width(2), .enable("false")) multiplexer_8 (
    .in0(out_11), .in1(adder_1_out), .out(multiplexer_8_out), .sel(and_18_out));
  Multiplexer #(.width(2), .enable("false")) multiplexer_9 (
    .in0(out_11), .in1(subtractor_1_out), .out(multiplexer_9_out), .sel(and_19_out));
  Multiplexer #(.width(2), .enable("false")) multiplexer_10 (
    .in0(out_10), .in1(subtractor_2_out), .out(multiplexer_10_out), .sel(and_20_out));
  Multiplexer #(.width(2), .enable("false")) multiplexer_11 (
    .in0(out_10), .in1(adder_2_out), .out(multiplexer_11_out), .sel(and_21_out));
  Subtractor #(.width(2)) subtractor_1 (.a(out_11), .b(2'b01), .out(subtractor_1_out));  // open: bin, bout
  Adder #(.width(2)) adder_1 (.a(2'b01), .b(out_11), .out(adder_1_out));  // open: cin, cout
  Subtractor #(.width(2)) subtractor_2 (.a(out_10), .b(2'b01), .out(subtractor_2_out));  // open: bin, bout
  Adder #(.width(2)) adder_2 (.a(2'b01), .b(out_10), .out(adder_2_out));  // open: cin, cout

  // Other names for the same wires on the sheet: col[1:0] = out_11; row[1:0] = out_10

  // Notes on the sheet:
  //   dir - 2
  //   dir - 3
  //   dir - 0
  //   dir - 1
endmodule

module field (
  input  [2:0] in_1,
  input  [3:0] in_2,
  input  [2:0] in_3,
  input  [3:0] in_4,
  input  [2:0] in_5,
  input  [3:0] in_6,
  input  [2:0] in_7,
  output [8:0] out_8,
  output [8:0] out_9,
  output [8:0] out_10,
  output [8:0] out_11,
  output [8:0] out_12,
  output [8:0] out_13,
  output [8:0] out_14,
  output [8:0] out_15,
  output [8:0] out_16
);


  assign out_8 = {9{1'b0}};
  assign out_9 = {2'b01, in_1[2], 1'b1, in_1[1], 1'b1, in_1[0], 2'b10};
  assign out_10 = {1'b0, in_2[3], 1'b0, in_2[2], 1'b0, in_2[1], 1'b0, in_2[0], 1'b0};
  assign out_11 = {2'b01, in_3[2], 1'b1, in_3[1], 1'b1, in_3[0], 2'b10};
  assign out_12 = {1'b0, in_4[3], 1'b0, in_4[2], 1'b0, in_4[1], 1'b0, in_4[0], 1'b0};
  assign out_13 = {2'b01, in_5[2], 1'b1, in_5[1], 1'b1, in_5[0], 2'b10};
  assign out_14 = {1'b0, in_6[3], 1'b0, in_6[2], 1'b0, in_6[1], 1'b0, in_6[0], 1'b0};
  assign out_15 = {2'b01, in_7[2], 1'b1, in_7[1], 1'b1, in_7[0], 2'b10};
  assign out_16 = {9{1'b0}};
endmodule
