// Logisim project lab_solution.circ as structural Verilog: 3 circuits, main circuit main
module main (
  input  [1:0] act,
  input  [2:0] r1,
  input  [3:0] r2,
  input  [2:0] r3,
  input  [3:0] r4,
  input  [2:0] r5,
  input  [3:0] r6,
  input  [2:0] r7,
  output [1:0] out_9,
  output [1:0] out_10
);

  wire active, and_1_out, and_2_out, and_3_out, clk, comparator_1_eq, d_ff_1_q, decoder_1_out0,
       decoder_1_out1, decoder_1_out2, decoder_1_out3, decoder_2_out0, decoder_2_out1, decoder_2_out2,
       decoder_2_out3, en, multiplexer_5_out, multiplexer_6_out, multiplexer_7_out, multiplexer_8_out,
       multiplexer_9_out, nand_1_out, or_1_out, or_2_out, or_3_out, or_5_out, rst, s_r_ff_1_q, start;
  wire [1:0] adder_1_out, adder_2_out, demultiplexer_1_out0, demultiplexer_1_out1, dir, multiplexer_3_out,
       multiplexer_10_out, multiplexer_11_out, multiplexer_12_out, multiplexer_13_out, not_1_out, not_4_out,
       register_1_q, register_2_q, register_3_q, subtractor_1_out;
  wire [2:0] multiplexer_4_out;
  wire [3:0] multiplexer_1_out, multiplexer_2_out;
  wire [8:0] field_1_out_8, field_1_out_9, field_1_out_10, field_1_out_11, field_1_out_12, field_1_out_13,
       field_1_out_14, field_1_out_15, field_1_out_16;

  // Probe on act
  Register #(.width(2)) register_1 (.D(act), .Q(register_1_q), .clk(clk), .clr(rst));  // open: en
  Multiplexer #(.select(2), .width(4), .enable("false")) multiplexer_1 (
    .in0(4'b0000), .in1(r2), .in2(r4), .in3(r6), .out(multiplexer_1_out), .sel(out_9));
  Multiplexer #(.select(2), .width(4), .enable("false")) multiplexer_2 (
    .in0(r2), .in1(r4), .in2(r6), .in3(4'b0000), .out(multiplexer_2_out), .sel(out_9));
  Clock u_clk (.out(clk));
  Button u_rst (.out(rst));
  Button u_start (.out(start));
  assign not_1_out = ~multiplexer_12_out;  // NOT_Gate not_1, 2 bits wide
  Register #(.width(2)) register_2 (.D(not_1_out), .en(en), .Q(register_2_q), .clk(clk), .clr(rst));
  assign out_9 = ~register_2_q;  // NOT_Gate not_2, 2 bits wide
  Register #(.width(2)) register_3 (.D(not_4_out), .en(en), .Q(register_3_q), .clk(clk), .clr(rst));
  assign out_10 = ~register_3_q;  // NOT_Gate not_3, 2 bits wide
  assign not_4_out = ~multiplexer_13_out;  // NOT_Gate not_4, 2 bits wide
  D_Flip_Flop d_ff_1 (.Q(d_ff_1_q), .preset(start), .reset(or_1_out));  // open: clk, D, Qn, en
  Multiplexer #(.select(2), .width(2)) multiplexer_3 (
    .in0(2'b01), .in1(2'b11), .in2(2'b10), .out(multiplexer_3_out), .sel(register_1_q), .en(s_r_ff_1_q));  // open: in3
  or or_1 (or_1_out, or_2_out, decoder_2_out3);
  and and_1 (and_1_out, act[0], act[1], start);
  Multiplexer #(.select(2), .width(3), .enable("false")) multiplexer_4 (
    .in0(r1), .in1(r3), .in2(r5), .in3(r7), .out(multiplexer_4_out), .sel(out_9));
  LED led_1 (.in(active));
  LED led_2 (.in(decoder_1_out3));
  Decoder #(.select(2), .disabled(0), .enable("false")) decoder_1 (
    .out0(decoder_1_out0), .out1(decoder_1_out1), .out2(decoder_1_out2), .out3(decoder_1_out3), .sel(dir));
  field field_1 (
    .in_1(r1), .in_2(r2), .in_3(r3), .in_4(r4), .in_5(r5), .in_6(r6), .in_7(r7), .out_8(field_1_out_8),
    .out_9(field_1_out_9), .out_10(field_1_out_10), .out_11(field_1_out_11), .out_12(field_1_out_12),
    .out_13(field_1_out_13), .out_14(field_1_out_14), .out_15(field_1_out_15), .out_16(field_1_out_16));
  DotMatrix #(.inputtype("row"), .matrixcols(9), .matrixrows(9)) dotmatrix_1 (
    .row0(field_1_out_8), .row1(field_1_out_9), .row2(field_1_out_10), .row3(field_1_out_11),
    .row4(field_1_out_12), .row5(field_1_out_13), .row6(field_1_out_14), .row7(field_1_out_15),
    .row8(field_1_out_16));
  // Probe on out_9
  // Probe on out_10
  Register #(.width(2)) register_4 (.D(adder_1_out), .en(or_2_out), .Q({dir[0], dir[1]}), .clk(clk));  // open: clr
  Adder #(.width(2)) adder_1 (.a({dir[0], dir[1]}), .b(multiplexer_3_out), .out(adder_1_out));  // open: cin, cout
  D_Flip_Flop d_ff_2 (.Q(en), .preset(and_1_out), .reset(or_3_out));  // open: clk, D, Qn, en
  Multiplexer #(.select(2), .enable("false")) multiplexer_5 (
    .in0(multiplexer_1_out[3]), .in1(multiplexer_1_out[2]), .in2(multiplexer_1_out[1]),
    .in3(multiplexer_1_out[0]), .out(multiplexer_5_out), .sel(out_10));
  Multiplexer #(.select(2), .enable("false")) multiplexer_6 (
    .in0(multiplexer_2_out[3]), .in1(multiplexer_2_out[2]), .in2(multiplexer_2_out[1]),
    .in3(multiplexer_2_out[0]), .out(multiplexer_6_out), .sel(out_10));
  Multiplexer #(.select(2), .enable("false")) multiplexer_7 (
    .in0(1'b0), .in1(multiplexer_4_out[2]), .in2(multiplexer_4_out[1]), .in3(multiplexer_4_out[0]),
    .out(multiplexer_7_out), .sel(out_10));
  Multiplexer #(.select(2), .enable("false")) multiplexer_8 (
    .in0(multiplexer_4_out[2]), .in1(multiplexer_4_out[1]), .in2(multiplexer_4_out[0]), .in3(1'b0),
    .out(multiplexer_8_out), .sel(out_10));
  LED led_3 (.in(decoder_1_out0));
  LED led_4 (.in(decoder_1_out2));
  LED led_5 (.in(decoder_1_out1));
  // Probe on {dir[0], dir[1]}
  or or_2 (or_2_out, decoder_2_out2, decoder_2_out1, decoder_2_out0);
  Decoder #(.select(2), .disabled(0)) decoder_2 (
    .out0(decoder_2_out0), .out1(decoder_2_out1), .out2(decoder_2_out2), .out3(decoder_2_out3),
    .sel(register_1_q), .en(s_r_ff_1_q));
  S_R_Flip_Flop s_r_ff_1 (.S(d_ff_1_q), .clk(clk), .R(or_1_out), .Q(s_r_ff_1_q), .reset(rst));  // open: Qn, preset, en
  or or_3 (or_3_out, rst, ~multiplexer_9_out);  // OR_Gate
  Multiplexer #(.select(2), .enable("false")) multiplexer_9 (
    .in0(multiplexer_5_out), .in1(multiplexer_6_out), .in2(multiplexer_8_out), .in3(multiplexer_7_out),
    .out(multiplexer_9_out), .sel(dir));
  nand nand_1 (nand_1_out, act[0], act[1]);
  Multiplexer #(.width(2)) multiplexer_10 (
    .in0(out_9), .in1(out_10), .out(multiplexer_10_out), .sel(dir[1]), .en(multiplexer_9_out));
  and and_2 (and_2_out, s_r_ff_1_q, nand_1_out);
  Adder #(.width(2)) adder_2 (.a(multiplexer_10_out), .b(2'b01), .out(adder_2_out));  // open: cin, cout
  Multiplexer #(.width(2), .enable("false")) multiplexer_11 (
    .in0(adder_2_out), .in1(subtractor_1_out), .out(multiplexer_11_out), .sel(comparator_1_eq));
  Subtractor #(.width(2)) subtractor_1 (.a(multiplexer_10_out), .b(2'b01), .out(subtractor_1_out));  // open: bin, bout
  Comparator #(.width(1)) comparator_1 (.a(dir[1]), .b(dir[0]), .eq(comparator_1_eq));  // open: gt, lt
  or or_4 (active, and_2_out, en);
  Demultiplexer #(.width(2), .enable("false")) demultiplexer_1 (
    .out0(demultiplexer_1_out0), .out1(demultiplexer_1_out1), .in(multiplexer_11_out), .sel(dir[1]));
  or or_5 (or_5_out, s_r_ff_1_q, dir[1]);
  Multiplexer #(.width(2), .enable("false")) multiplexer_12 (
    .in0(demultiplexer_1_out0), .in1(out_9), .out(multiplexer_12_out), .sel(or_5_out));
  Multiplexer #(.width(2), .enable("false")) multiplexer_13 (
    .in0(out_10), .in1(demultiplexer_1_out1), .out(multiplexer_13_out), .sel(and_3_out));
  and and_3 (and_3_out, dir[1], ~s_r_ff_1_q);  // AND_Gate

  // Other names for the same wires on the sheet: col[1:0] = out_10; row[1:0] = out_9
endmodule

module field (
  input  [2:0] in_1,
  input  [3:0] in_2,
  input  [2:0] in_3,
  input  [3:0] in_4,
  input  [2:0] in_5,
  input  [3:0] in_6,
  input  [2:0] in_7,
  output [8:0] out_8,
  output [8:0] out_9,
  output [8:0] out_10,
  output [8:0] out_11,
  output [8:0] out_12,
  output [8:0] out_13,
  output [8:0] out_14,
  output [8:0] out_15,
  output [8:0] out_16
);


  assign out_8 = {9{1'b0}};
  assign out_9 = {2'b01, in_1[2], 1'b1, in_1[1], 1'b1, in_1[0], 2'b10};
  assign out_10 = {1'b0, in_2[3], 1'b0, in_2[2], 1'b0, in_2[1], 1'b0, in_2[0], 1'b0};
  assign out_11 = {2'b01, in_3[2], 1'b1, in_3[1], 1'b1, in_3[0], 2'b10};
  assign out_12 = {1'b0, in_4[3], 1'b0, in_4[2], 1'b0, in_4[1], 1'b0, in_4[0], 1'b0};
  assign out_13 = {2'b01, in_5[2], 1'b1, in_5[1], 1'b1, in_5[0], 2'b10};
  assign out_14 = {1'b0, in_6[3], 1'b0, in_6[2], 1'b0, in_6[1], 1'b0, in_6[0], 1'b0};
  assign out_15 = {2'b01, in_7[2], 1'b1, in_7[1], 1'b1, in_7[0], 2'b10};
  assign out_16 = {9{1'b0}};
endmodule

module scheme (
  input  clk,
  input  rst,
  input  start,
  input  [1:0] act,
  input  [2:0] r1,
  input  [3:0] r2,
  input  [2:0] r3,
  input  [3:0] r4,
  input  [2:0] r5,
  input  [3:0] r6,
  input  [2:0] r7,
  output [1:0] row,
  output [1:0] col,
  output [1:0] dir,
  output active
);

  Register #(.width(2)) register_1 (.Q(row), .clk(clk));  // open: D, en, clr
  D_Flip_Flop d_ff_1 (.Q(active), .preset(start));  // open: clk, D, Qn, en, reset
  Register #(.width(2)) register_2 (.Q(col));  // open: D, en, clk, clr
  Register #(.width(2)) register_3 (.Q(dir));  // open: D, en, clk, clr
endmodule
